# Fritzing sketch ECE_206_Lab3-1 (saved by Fritzing 0.9.4)
breadboards: 1

parts:
  Part1 = Arduino Nano Every
  LED1 = 2-digit 7-segment (D2601) [package=THT-longpads]
  R2 = Resistor [tolerance=±5% resistance=100 package=THT]
  R1 = Resistor [tolerance=±5% resistance=100 package=THT]
  R3 = Resistor [tolerance=±5% resistance=100 package=THT]
  R4 = Resistor [tolerance=±5% resistance=100 package=THT]
  R5 = Resistor [tolerance=±1% resistance=100 package=THT]
  R6 = Resistor [tolerance=±5% resistance=100 package=THT]
  R7 = Resistor [tolerance=±5% resistance=100 package=THT]
  R8 = Resistor [tolerance=±5% resistance=100 package=THT]
  RE1 = Rotary Encoder [package=THT]
  R9 = Resistor [tolerance=±5% resistance=10k package=THT]
  R10 = Resistor [tolerance=±5% resistance=10k package=THT]

nets:
  N1: Part1.RESET, Part1.A7
  GND: Part1.GND, Part1.D13~, RE1.EncoderPinC
  N2: Part1.D2, R1.Pin_0
  N3: Part1.D3~, R2.Pin_0
  N4: Part1.D4, R3.Pin_0
  N5: Part1.D5~, R4.Pin_0
  N6: Part1.D6~, R5.Pin_0
  N7: Part1.D7, R6.Pin_0
  N8: Part1.D8, R7.Pin_0
  N9: Part1.D9~, R8.Pin_0
  N10: Part1.D11/MOSI, Part1.+5V, R9.Pin_1, R10.Pin_1
  N11: Part1.A6, RE1.EncoderPinB, R9.Pin_0
  N12: Part1.A4, RE1.EncoderPinA, R10.Pin_0
  N13: Part1.A3, LED1.DIG1
  N14: Part1.A2, LED1.DIG2
  N15: LED1.A, R6.Pin_1
  N16: LED1.C, R3.Pin_1
  N17: LED1.DP, R5.Pin_1
  N18: LED1.E, R1.Pin_1
  N19: LED1.D, R2.Pin_1
  N20: LED1.G, R4.Pin_1
  N21: LED1.F, R8.Pin_1
  N22: LED1.B, R7.Pin_1

custom parts:
  Arduino Nano Every: The Nano Every is Arduino’s 5V compatible board in the smallest available form factor: 45x18mm! The Arduino Nano is the preferred board for many projects requiring a small and easy to use microcontroller board. The small footprint and low price, make the Nano Every particularly suited for wearable inventions, low cost robotics, electronic musical instruments, and general use to control smaller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
  2-digit 7-segment (D2601): Most common two-digit seven-segment led indicator you can find on the internet. 10 legs: 2 common electrodes (one per each digit), 8 electrodes of each segment. This variant has been modified by Zuofu Cheng to reflect the D2601 pinout.
