# Fritzing sketch ECE_206_Lab6 (saved by Fritzing 0.9.4)
breadboards: 1

parts:
  Part1 = Arduino Nano Every
  Q1 = Basic FET N-Channel [package="TO220 [THT]"]
  Q2 = Basic FET N-Channel [package="TO220 [THT]"]
  Q3 = Basic FET P-Channel [package="TO220 [THT]"]
  Q4 = Basic FET P-Channel [package="TO220 [THT]"]
  DC_Mot_Enc1 = DC Motor with two-phase hall-encoder [part_number=ROB-16413]

nets:
  N1: Part1.RESET, Part1.A7
  N2: Part1.GND, Part1.D13~, Q1.source, Q2.source
  N3: Part1.D3~, Q1.gate, Q4.gate
  N4: Part1.D4, Q2.gate, Q3.gate
  N5: Part1.D11/MOSI, Part1.+5V, Q3.source, Q4.source
  N6: Q1.drain, Q4.drain, DC_Mot_Enc1.pin2
  N7: Q2.drain, Q3.drain, DC_Mot_Enc1.pin1

custom parts:
  Arduino Nano Every: The Nano Every is Arduino’s 5V compatible board in the smallest available form factor: 45x18mm! The Arduino Nano is the preferred board for many projects requiring a small and easy to use microcontroller board. The small footprint and low price, make the Nano Every particularly suited for wearable inventions, low cost robotics, electronic musical instruments, and general use to control smaller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
  DC Motor with two-phase hall-encoder: DC Motor with two-phase hall-encoder. Modified by Zuofu Cheng for the Sparkfun hobby motor with encoder. Original found at: https://github.com/TobiasWeis/pypibot/blob/master/docs/diagrams/Fritzing_Part_DC_Motor_Encoder/DC%20Motor%20with%20two-phase%20hall-encoder.fzpz
